# Fritzing sketch ultimateGPStrackerBreadboardLayout.3 (saved by Fritzing 1.0.6)
breadboards: 2

parts:
  Mod1 = Raspberry Pi Pico W
  Part1 = Adafruit Ultimate GPS v3 [part_number="Adafruit #746"]
  Squix1 = OLED 0.96" 128x64 I2C SSD1306 (GND/VCC)
  S1 = Momentary Switch [package=ksa_sealed_tac_switch]
  S2 = Momentary Switch [package=ksa_sealed_tac_switch]
  S3 = Momentary Switch [package=ksa_sealed_tac_switch]
  M1 = RioRand LM2596
  BAT1 = Battery Holders [package=lipo-1100mAh]
  SD_card_module1 = SD Card Module
  S4 = Toggle Switch [package=THT]

nets:
  N1: Mod1.pin_3, Mod1.pin_8, Mod1.pin_13, Mod1.pin_18, Mod1.pin_23, Mod1.pin_28, Mod1.pin_33, Mod1.pin_38, Mod1.pin_42, Part1.GND
  N2: Mod1.pin_4, Squix1.SCA
  N3: Mod1.pin_5, Squix1.SCL
  N4: Mod1.pin_11, Part1.RX
  N5: Mod1.pin_14, S2.1
  N6: Mod1.pin_15, S1.3
  N7: Mod1.pin_16, SD_card_module1.MISO
  N8: Mod1.pin_17, SD_card_module1.CS
  N9: Mod1.pin_19, Mod1.pin_20, SD_card_module1.MOSI, SD_card_module1.SCK
  N10: Mod1.pin_30, S3.1
  N11: Mod1.pin_39, Part1.VIN, M1.Pin_3
  GND: Squix1.GND, S2.4, S3.4, SD_card_module1.GND
  N12: Squix1.VCC, SD_card_module1.+3.3, SD_card_module1.+5
  N13: M1.Pin_1, S4.L2
  N14: BAT1.+, S4.COM

notes:
  GND
  +5V
  +3.7V
  B1
  B2
  Reset
  +3.3V
  R

custom parts:
  Raspberry Pi Pico W: Raspberry Pi Pico W. Based around the RP2040 microcontroller the Pico W is a low cost microcontroller device bringing Raspberry Pi quality, cost, and easy of use to the microcontroller space. The areas marked KEEPOUT in pcb silkscreen should not have traces running through them to avoid shorts on a soldered in module!
  Adafruit Ultimate GPS v3: We carry a few different GPS modules here in the Adafruit shop, but none that satisfied our every desire - that's why we designed this little GPS breakout board. We believe this is the Ultimate GPS module, so we named it that. It's got everything you want and more: -165 dBm sensitivity, 10 Hz updates, 66 channels 5V friendly design and only 20mA current draw Breadboard friendly + two mounting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
  OLED 0.96" 128x64 I2C SSD1306 (GND/VCC): OLED 0.96" 128x64 I2C SSD1306 Pinout: GND/VCC/SCL/SDA
  SD Card Module: SD Card Module Slot Socket Reader For Arduino ARM MCU
