# Fritzing sketch ultimateGPStrackerBreadboardLayout (saved by Fritzing 0.9.6b)
breadboards: 2

parts:
  Mod1 = Raspberry Pi Pico W
  Part1 = Adafruit Ultimate GPS v3 [part_number="Adafruit #746"]
  Squix1 = OLED 0.96" 128x64 I2C SSD1306 (GND/VCC)
  S1 = Momentary Switch [package=ksa_sealed_tac_switch]
  S2 = Momentary Switch [package=ksa_sealed_tac_switch]
  S3 = Momentary Switch [package=ksa_sealed_tac_switch]
  SD_card_module1 = SD Card Module

nets:
  N1: Mod1.pin_3, Mod1.pin_8, Mod1.pin_13, Mod1.pin_18, Mod1.pin_23, Mod1.pin_28, Mod1.pin_33, Mod1.pin_38, Part1.GND
  N2: Mod1.pin_4, Squix1.SCA
  N3: Mod1.pin_5, Squix1.SCL
  N4: Mod1.pin_11, Part1.RX
  N5: Mod1.pin_15, S1.3
  N6: Mod1.pin_16, SD_card_module1.MISO
  N7: Mod1.pin_17, SD_card_module1.CS
  N8: Mod1.pin_20, SD_card_module1.MOSI, SD_card_module1.SCK
  N9: Mod1.pin_30, S3.1
  N10: Mod1.pin_39, Part1.VIN
  GND: Squix1.GND, S2.4, S3.4, SD_card_module1.GND
  N11: Squix1.VCC, SD_card_module1.+3.3, SD_card_module1.+5

custom parts:
  Raspberry Pi Pico W: Raspberry Pi Pico W. Based around the RP2040 microcontroller the Pico W is a low cost microcontroller device bringing Raspberry Pi quality, cost, and easy of use to the microcontroller space. The areas marked KEEPOUT in pcb silkscreen should not have traces running through them to avoid shorts on a soldered in module!
  Adafruit Ultimate GPS v3: We carry a few different GPS modules here in the Adafruit shop, but none that satisfied our every desire - that's why we designed this little GPS breakout board. We believe this is the Ultimate GPS module, so we named it that. It's got everything you want and more: -165 dBm sensitivity, 10 Hz updates, 66 channels 5V friendly design and only 20mA current draw Breadboard friendly + two mounting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
  OLED 0.96" 128x64 I2C SSD1306 (GND/VCC): OLED 0.96" 128x64 I2C SSD1306 Pinout: GND/VCC/SCL/SDA
  SD Card Module: SD Card Module Slot Socket Reader For Arduino ARM MCU
